# Fritzing sketch plant_game_circuit (saved by Fritzing 0.7.4b)
breadboards: 1

parts:
  Arduino1 = Arduino
  LED1 = LED - 5mm [color="Red (633nm)" package="5 mm [THT]"]
  P1_Health = LED - 5mm [color="Red (633nm)" package="5 mm [THT]"]
  LED3 = LED - 5mm [color="Red (633nm)" package="5 mm [THT]"]
  LED4 = LED - 5mm [color="Red (633nm)" package="5 mm [THT]"]
  P2_Health = LED - 5mm [color="Red (633nm)" package="5 mm [THT]"]
  LED6 = LED - 5mm [color="Red (633nm)" package="5 mm [THT]"]
  R1 = Resistor [tolerance=±5% resistance=220 package=THT]
  R2 = Resistor [tolerance=±5% resistance=220 package=THT]
  R3 = Resistor [tolerance=±5% resistance=220 package=THT]
  R4 = Resistor [tolerance=±5% resistance=220 package=THT]
  R5 = Resistor [tolerance=±5% resistance=220 package=THT]
  R6 = Resistor [tolerance=±5% resistance=220 package=THT]
  P1_Bomb = Pushbutton [package="[THT]"]
  P1_Defend = Pushbutton [package="[THT]"]
  P2_Bomb = Pushbutton [package="[THT]"]
  P2_Defend = Pushbutton [package="[THT]"]
  R7 = Resistor [tolerance=±5% resistance=220 package=THT]
  R8 = Resistor [tolerance=±5% resistance=220 package=THT]
  R9 = Resistor [tolerance=±5% resistance=220 package=THT]
  R10 = Resistor [tolerance=±5% resistance=220 package=THT]
  LED7 = LED - 5mm [color="Red (633nm)" package="5 mm [THT]"]
  R11 = Resistor [tolerance=±5% resistance=220 package=THT]

nets:
  N1: Arduino1.D11, R6.Pin_1
  N2: Arduino1.D10, R5.Pin_1
  N3: Arduino1.D9, R4.Pin_1
  N4: Arduino1.D8, R3.Pin_1
  N5: Arduino1.D7, R2.Pin_1
  N6: Arduino1.D6, R1.Pin_1
  N7: Arduino1.D5, P2_Defend.Pin_1, P2_Defend.Pin_2, R10.Pin_1
  N8: Arduino1.D4, P2_Bomb.Pin_1, P2_Bomb.Pin_2, R9.Pin_1
  N9: Arduino1.D3, P1_Bomb.Pin_1, P1_Bomb.Pin_2, R7.Pin_1
  N10: Arduino1.D2, P1_Defend.Pin_1, P1_Defend.Pin_2, R8.Pin_1
  N11: Arduino1.+5V, P1_Bomb.Pin_3, P1_Bomb.Pin_4, P1_Defend.Pin_3, P1_Defend.Pin_4, P2_Bomb.Pin_3, P2_Bomb.Pin_4, P2_Defend.Pin_3, P2_Defend.Pin_4
  N12: Arduino1.GND, LED1.anode, P1_Health.anode, LED3.anode, LED4.anode, P2_Health.anode, LED6.anode, R7.Pin_0, R8.Pin_0, R9.Pin_0, R10.Pin_0, LED7.anode
  N13: Arduino1.A5, R11.Pin_1
  N14: LED1.cathode, R1.Pin_0
  N15: P1_Health.cathode, R2.Pin_0
  N16: LED3.cathode, R3.Pin_0
  N17: LED4.cathode, R4.Pin_0
  N18: P2_Health.cathode, R5.Pin_0
  N19: LED6.cathode, R6.Pin_0
  N20: LED7.cathode, R11.Pin_0
